# Fritzing sketch MazeUnlockTransmitterScheme (saved by Fritzing 0.9.3b)
breadboards: 1

parts:
  Součástka1 = Arduino Nano (Rev3.0)
  Součástka2 = Thumb Joystick
  Součástka3 = NRF24L01+ Breakout Board
  J1 = Piezo Speaker
  LED2 = LED - 3mm [color="Green (555nm)" package="3 mm [THT]"]
  LED1 = LED - 3mm [color="Red (633nm)" package="3 mm [THT]"]
  SW3 = DIP Switch 8 Position [package=dipswitch-08]

nets:
  N1: Součástka1.D3, Součástka2.SEL
  N2: Součástka1.D4, LED2.anode
  N3: Součástka1.D5, LED1.anode
  N4: Součástka1.D6, J1.pin2
  N5: Součástka1.D7, SW3.16
  N6: Součástka1.D8, Součástka3.CS
  N7: Součástka1.D9, Součástka3.CE
  N8: Součástka1.D11/MOSI, Součástka3.MOSI
  N9: Součástka1.D12/MISO, Součástka3.MISO
  GND: Součástka1.GND, Součástka2.GND, Součástka3.GND, J1.pin1, LED2.cathode, LED1.cathode
  5V: Součástka1.5V, Součástka2.VCC, SW3.1
  N10: Součástka1.A6, Součástka2.HORZ
  N11: Součástka1.A5, Součástka2.VERT
  N12: Součástka1.A2, SW3.13
  N13: Součástka1.A1, SW3.14
  N14: Součástka1.A0, SW3.15
  3V3: Součástka1.3V3, Součástka3.VCC
  N15: Součástka1.D13/SCK, Součástka3.SCK
